# Fritzing sketch BH1745NUC (saved by Fritzing 0.9.5d)

parts:
  Raspberry_Pi_1 = Raspberry Pi 3 [part_number=RPI-3-V1.2]
  Conta1 = BH1745NUC

nets:
  3V3: Raspberry_Pi_1.3v3, Conta1.3.3V
  N1: Raspberry_Pi_1.GPIO2, Conta1.SDA
  N2: Raspberry_Pi_1.GPIO3, Conta1.SCL
  GND: Raspberry_Pi_1.GND, Conta1.GND
